// Logisim project Project3Given.circ as structural Verilog: 9 circuits, main circuit CPU15
module main (
  input  EnableBreakpoint,
  input  [14:0] Breakpoint
);

  wire and_2_out, and_3_out, chipset_1_irq, CLK, clock_1_out, cpu15_1_c, cpu15_1_n, cpu15_1_o, cpu15_1_z,
       KBCLR, KBIRQ, KBRD, MEMCS, nand_1_out, RE, TTYCLR, TTYWE, undriven, undriven_2, WE;
  wire [6:0] KBDATA, TTYDATA;
  wire [7:0] cpu15_1_srf;
  wire [14:0] ADDR, chipset_1_ivect, chipset_1_led0, chipset_1_led1, chipset_1_led2, chipset_1_led3,
       chipset_1_led4, chipset_1_led5, chipset_1_led6, chipset_1_led7, chipset_1_led8, chipset_1_led9,
       chipset_1_leda, chipset_1_ledb, chipset_1_ledc, chipset_1_ledd, chipset_1_lede, cpu15_1_ib,
       cpu15_1_pc, cpu15_1_r0, cpu15_1_r1, cpu15_1_r2, cpu15_1_r3, cpu15_1_r4, cpu15_1_r5, cpu15_1_r6,
       cpu15_1_r7, cpu15_1_srp, DATA, xnor_1_out;

  Clock clock_1 (.out(clock_1_out));
  nand nand_1 (nand_1_out, EnableBreakpoint, xnor_1_out[0], xnor_1_out[1], xnor_1_out[2], xnor_1_out[3], xnor_1_out[4], xnor_1_out[5], xnor_1_out[6], xnor_1_out[7], xnor_1_out[8], xnor_1_out[9], xnor_1_out[10], xnor_1_out[11], xnor_1_out[12], xnor_1_out[13], xnor_1_out[14], 1'b1);
  and and_1 (CLK, clock_1_out, nand_1_out);
  assign xnor_1_out = ~(Breakpoint ^ cpu15_1_pc);  // XNOR_Gate xnor_1, 15 bits wide
  LED I (.in(cpu15_1_z));
  LED Z (.in(undriven));
  LED N (.in(cpu15_1_n));
  LED O (.in(undriven_2));
  LED C (.in(cpu15_1_o));
  LED E (.in(cpu15_1_c));
  and and_2 (and_2_out, WE, MEMCS);
  and and_3 (and_3_out, MEMCS, RE);
  RAM #(.addrWidth(15), .asyncread("true"), .dataWidth(15), .databus("bidir")) ram_1 (
    .addr(ADDR), .we(and_2_out), .oe(and_3_out), .clk(CLK));  // open: data
  // Probe on cpu15_1_pc
  // Probe on cpu15_1_ib
  // Probe on cpu15_1_srp
  // Probe on cpu15_1_srf
  // Probe on cpu15_1_r0
  // Probe on cpu15_1_r1
  // Probe on cpu15_1_r2
  // Probe on cpu15_1_r3
  // Probe on cpu15_1_r4
  // Probe on cpu15_1_r5
  // Probe on cpu15_1_r6
  // Probe on cpu15_1_r7
  CPU15 cpu15_1 (
    .Z(cpu15_1_z), .in_2(undriven), .N(cpu15_1_n), .in_3(undriven_2), .O(cpu15_1_o), .C(cpu15_1_c),
    .PC(cpu15_1_pc), .IB(cpu15_1_ib), .SRP(cpu15_1_srp), .SRF(cpu15_1_srf), .R0(cpu15_1_r0), .R1(cpu15_1_r1),
    .R2(cpu15_1_r2), .R3(cpu15_1_r3), .R4(cpu15_1_r4), .R5(cpu15_1_r5), .R6(cpu15_1_r6), .R7(cpu15_1_r7),
    .CLK(CLK), .IRQ(chipset_1_irq), .RE(RE), .WE(WE), .ADDR(ADDR), .DATAIN(DATA), .DATAOUT(DATA));  // open: I, in_1, E
  // Probe on ADDR
  // Probe on DATA
  // Probe on chipset_1_ivect
  // Probe on TTYDATA
  CHIPSET chipset_1 (
    .RE(RE), .WE(WE), .ADDR(ADDR), .CPUDATAIN(DATA), .CPUDATAOUT(DATA), .IRQ(chipset_1_irq),
    .IVECT(chipset_1_ivect), .CLK(CLK), .MEMCS(MEMCS), .TTYWR(TTYWE), .TTYCLR(TTYCLR), .TTYDATA(TTYDATA),
    .KBRD(KBRD), .KBCLR(KBCLR), .KBIRQ(KBIRQ), .KBDATA(KBDATA), .LED0(chipset_1_led0), .LED1(chipset_1_led1),
    .LED2(chipset_1_led2), .LED3(chipset_1_led3), .LED4(chipset_1_led4), .LED5(chipset_1_led5),
    .LED6(chipset_1_led6), .LED7(chipset_1_led7), .LED8(chipset_1_led8), .LED9(chipset_1_led9),
    .LEDA(chipset_1_leda), .LEDB(chipset_1_ledb), .LEDC(chipset_1_ledc), .LEDD(chipset_1_ledd),
    .LEDE(chipset_1_lede));
  TTY tty_1 (.data(TTYDATA), .clk(CLK), .we(TTYWE), .clr(TTYCLR));
  Keyboard keyboard_1 (.clk(CLK), .re(KBRD), .clr(KBCLR), .avail(KBIRQ), .data(KBDATA));
  DotMatrix #(.matrixcols(15), .matrixrows(15)) dotmatrix_1 (
    .col0(chipset_1_led0), .col1(chipset_1_led1), .col2(chipset_1_led2), .col3(chipset_1_led3),
    .col4(chipset_1_led4), .col5(chipset_1_led5), .col6(chipset_1_led6), .col7(chipset_1_led7),
    .col8(chipset_1_led8), .col9(chipset_1_led9), .col10(chipset_1_leda), .col11(chipset_1_ledb),
    .col12(chipset_1_ledc), .col13(chipset_1_ledd), .col14(chipset_1_lede));
endmodule

// CPU
module CPU15 (
  input  in_1,
  input  in_2,
  input  in_3,
  input  [14:0] DATAIN,
  input  CLK,
  input  IRQ,
  output [14:0] PC,
  output [14:0] IB,
  output [14:0] SRP,
  output [7:0] SRF,
  output [14:0] R0,
  output [14:0] R1,
  output [14:0] R2,
  output [14:0] R3,
  output [14:0] R4,
  output [14:0] R5,
  output [14:0] R6,
  output [14:0] R7,
  output RE,
  output WE,
  output I,
  output Z,
  output [14:0] ADDR,
  output N,
  output O,
  output C,
  output E,
  output [14:0] DATAOUT
);

  wire and_1_out, CIN, ExecuteWriteback, FetchDecode, LOAD, OIN, REGW, SRFW, SRPW, STORE, SWI;
  wire [1:0] ASEL, BSEL, FLAGSRC;
  wire [2:0] ALUOP, REGDATASRC, RegsData, SelA, SelB, SelD, SelectA, SelectB, SelectD;
  wire [4:0] OPCODE;
  wire [7:0] FLAGWM, NF, WM;
  wire [14:0] A, ALU, B, D, DSRF, DSRP, F, IM, IncrementPC, INST, MEMORY, RegisterA, RegisterB, SEXT;

  Register #(.width(1)) register_1 (.Q(ExecuteWriteback), .clk(CLK));  // open: D, en, clr
  Register #(.width(15)) register_2 (.D(PC), .en(FetchDecode), .Q(ADDR), .clk(CLK));  // open: clr
  Register #(.width(15)) register_3 (.D(DATAIN), .en(FetchDecode), .Q(IB), .clk(CLK));  // open: clr
  not not_1 (FetchDecode, ExecuteWriteback);
  Register #(.width(15)) register_4 (.en(ExecuteWriteback), .Q(PC), .clk(CLK));  // open: D, clr
  and and_1 (and_1_out, ExecuteWriteback, LOAD);
  and and_2 (WE, ExecuteWriteback, STORE);
  or or_1 (RE, FetchDecode, and_1_out);
  assign DATAOUT = B;  // Buffer buffer_1, 15 bits wide
  // FLAGS8 flags8_1: pin names not known; wires that end beside it: IRQ, NF, WM, CLK, F
  ADDER15 adder15_1 (.A(PC), .B(15'h1), .S(IncrementPC));  // open: CIN, COUT
  REGS15 regs15_1 (
    .D(D), .W(in_3), .SelD(SelD), .CLK(CLK), .SelA(SelA), .SelB(SelB), .R0(R0), .R1(R1), .R2(R2), .R3(R3),
    .R4(R4), .R5(R5), .R6(R6), .R7(R7), .A(A), .B(B));
  Multiplexer #(.width(3)) multiplexer_1 (.in1(IB[7:5]), .out(SelectD), .sel(in_3));  // open: in0
  Multiplexer #(.select(2), .width(3)) multiplexer_2 (
    .in1(IB[10:8]), .out(SelectA), .sel(ASEL));  // open: in0, in2, in3
  Multiplexer #(.select(2), .width(3)) multiplexer_3 (
    .in1(IB[13:11]), .out(SelectB), .sel(BSEL));  // open: in0, in2, in3
  Multiplexer #(.select(2), .width(15)) multiplexer_4 (
    .in0(PC), .in1(A), .out(RegisterA), .sel(ASEL));  // open: in2, in3
  ALU15 alu15_1 (.A(A), .B(B), .OP(ALUOP), .CIN(CIN), .OIN(OIN), .R(ALU), .C(C), .O(O), .N(N), .Z(Z));
  DECODE15 decode15_1 (
    .OPCODE(OPCODE), .SWI(SWI), .STORE(STORE), .LOAD(LOAD), .ASEL(ASEL), .BSEL(BSEL), .ALUOP(ALUOP),
    .REGDATASRC(REGDATASRC), .REGW(REGW), .FLAGSRC(FLAGSRC), .FLAGWM(FLAGWM), .SRPW(SRPW), .SRFW(SRFW));
  IMM15 imm15_1 (.INST(INST), .SEXT(SEXT));
  Multiplexer #(.select(3), .width(15)) multiplexer_5 (
    .in0(ALU), .in1(MEMORY), .in2(IncrementPC), .in4(F), .in5(DSRP), .in6(DSRF), .in7(IM), .out(D),
    .sel(RegsData));  // open: in3
  Multiplexer #(.select(2), .width(15)) multiplexer_6 (
    .in0(PC), .in1(B), .out(RegisterB), .sel(BSEL));  // open: in2, in3

  assign E = in_2;
  assign I = in_1;

  // Other names for the same wires on the sheet: DATA[14:0] = DATAIN; W = in_3

  // Notes on the sheet:
  //   For choosing the states
  //   Feed ADDR value in the PC
  //   Data goes through the instruction buffer and updates
  //   Write Enable
  //   Counting program
  //   Read Enable
  //   Data should go out once write enable is true
  //   PC Increments by +1
  //   Select D
  //   Select A
  //   Select B
  //   REGISTER
  //   FLAGS
  //   A Register
  //   DECODER
  //   IMM
  //   ALU
  //   Register Data
  //   B Register
endmodule

module CHIPSET (
  input  RE,
  input  WE,
  input  [14:0] ADDR,
  input  [14:0] CPUDATAIN,
  input  KBIRQ,
  input  [6:0] KBDATA,
  input  CLK,
  output MEMCS,
  output TTYWR,
  output [14:0] IVECT,
  output TTYCLR,
  output [6:0] TTYDATA,
  output KBRD,
  output KBCLR,
  output [14:0] CPUDATAOUT,
  output IRQ,
  output [14:0] LED0,
  output [14:0] LED1,
  output [14:0] LED2,
  output [14:0] LED3,
  output [14:0] LED4,
  output [14:0] LED5,
  output [14:0] LED6,
  output [14:0] LED7,
  output [14:0] LED8,
  output [14:0] LED9,
  output [14:0] LEDA,
  output [14:0] LEDB,
  output [14:0] LEDC,
  output [14:0] LEDD,
  output [14:0] LEDE
);

  wire and_1_out, and_8_out, and_10_out, DATA7, IOCS, IVECTADDR, IVECTEN, IVECTRE, KBCS, LED0EN, LED0END,
       LED1EN, LED1END, LED2EN, LED2END, LED3EN, LED3END, LED4EN, LED4END, LED5EN, LED5END, LED6EN, LED6END,
       LED7EN, LED7END, LED8EN, LED8END, LED9EN, LED9END, LEDAEN, LEDAEND, LEDBEN, LEDBEND, LEDCEN, LEDCEND,
       LEDCS, LEDDEN, LEDDEND, LEDEEN, LEDEEND, LEDFEND, LEDRE, multiplexer_17_out, multiplexer_18_out, RWE,
       TTYCS;
  wire [14:0] DATAL0, DATAL1, DATAL2, DATAL3, DATAL4, DATAL5, DATAL6, DATAL7, DATAL8, DATAL9, DATALA, DATALB,
       DATALC, DATALD, DATALE, LEDDATA;
  wire [14:8] KBDATA15;

  assign CPUDATAOUT = KBRD ? {KBDATA15, DATA7, KBDATA} : 15'bz;  // Controlled_Buffer controlled_buffer_1
  assign CPUDATAOUT = LEDRE ? LEDDATA : 15'bz;  // Controlled_Buffer controlled_buffer_2
  assign CPUDATAOUT = IVECTRE ? IVECT : 15'bz;  // Controlled_Buffer controlled_buffer_3
  Register #(.width(15)) register_1 (.D(DATAL0), .en(LED0EN), .Q(LED0), .clk(CLK));  // open: clr
  Register #(.width(15)) register_2 (.D(DATAL1), .en(LED1EN), .Q(LED1), .clk(CLK));  // open: clr
  Register #(.width(15)) register_3 (.D(DATAL2), .en(LED2EN), .Q(LED2), .clk(CLK));  // open: clr
  Register #(.width(15)) register_4 (.D(DATAL3), .en(LED3EN), .Q(LED3), .clk(CLK));  // open: clr
  Register #(.width(15)) register_5 (.D(DATAL4), .en(LED4EN), .Q(LED4), .clk(CLK));  // open: clr
  and and_1 (and_1_out, WE, LEDCS);
  Decoder #(.select(4)) decoder_1 (
    .out0(LED0END), .out1(LED1END), .out2(LED2END), .out3(LED3END), .out4(LED4END), .out5(LED5END),
    .out6(LED6END), .out7(LED7END), .out8(LED8END), .out9(LED9END), .out10(LEDAEND), .out11(LEDBEND),
    .out12(LEDCEND), .out13(LEDDEND), .out14(LEDEEND), .out15(LEDFEND), .sel(ADDR[3:0]), .en(and_1_out));
  Register #(.width(15)) register_6 (.D(DATAL5), .en(LED5EN), .Q(LED5), .clk(CLK));  // open: clr
  Register #(.width(15)) register_7 (.D(DATAL6), .en(LED6EN), .Q(LED6), .clk(CLK));  // open: clr
  Register #(.width(15)) register_8 (.D(DATAL7), .en(LED7EN), .Q(LED7), .clk(CLK));  // open: clr
  Register #(.width(15)) register_9 (.D(DATAL8), .en(LED8EN), .Q(LED8), .clk(CLK));  // open: clr
  Register #(.width(15)) register_10 (.D(DATAL9), .en(LED9EN), .Q(LED9), .clk(CLK));  // open: clr
  or or_1 (LED0EN, LED0END, LEDFEND);
  or or_2 (LED1EN, LED1END, LEDFEND);
  or or_3 (LED2EN, LED2END, LEDFEND);
  or or_4 (LED3EN, LED3END, LEDFEND);
  or or_5 (LED4EN, LED4END, LEDFEND);
  or or_6 (LED5EN, LED5END, LEDFEND);
  or or_7 (LED6EN, LED6END, LEDFEND);
  or or_8 (LED7EN, LED7END, LEDFEND);
  or or_9 (LED8EN, LED8END, LEDFEND);
  or or_10 (LED9EN, LED9END, LEDFEND);
  or or_11 (LEDAEN, LEDAEND, LEDFEND);
  or or_12 (LEDBEN, LEDBEND, LEDFEND);
  or or_13 (LEDCEN, LEDCEND, LEDFEND);
  or or_14 (LEDDEN, LEDDEND, LEDFEND);
  or or_15 (LEDEEN, LEDEEND, LEDFEND);
  Pull_Resistor pull_resistor_1 (.node(KBDATA15[14]));
  Pull_Resistor pull_resistor_2 (.node(KBDATA15[13]));
  Pull_Resistor pull_resistor_3 (.node(KBDATA15[12]));
  Pull_Resistor pull_resistor_4 (.node(KBDATA15[11]));
  Pull_Resistor pull_resistor_5 (.node(KBDATA15[10]));
  Pull_Resistor pull_resistor_6 (.node(KBDATA15[9]));
  Pull_Resistor pull_resistor_7 (.node(KBDATA15[8]));
  Pull_Resistor pull_resistor_8 (.node(DATA7));
  Register #(.width(15)) register_11 (.D(DATALA), .en(LEDAEN), .Q(LEDA), .clk(CLK));  // open: clr
  Register #(.width(15)) register_12 (.D(DATALB), .en(LEDBEN), .Q(LEDB), .clk(CLK));  // open: clr
  Register #(.width(15)) register_13 (.D(DATALC), .en(LEDCEN), .Q(LEDC), .clk(CLK));  // open: clr
  Register #(.width(15)) register_14 (.D(DATALD), .en(LEDDEN), .Q(LEDD), .clk(CLK));  // open: clr
  Register #(.width(15)) register_15 (.D(DATALE), .en(LEDEEN), .Q(LEDE), .clk(CLK));  // open: clr
  Multiplexer #(.width(15)) multiplexer_1 (.in0(CPUDATAIN), .in1(LED1), .out(DATAL0), .sel(LEDFEND));
  Multiplexer #(.width(15)) multiplexer_2 (.in0(CPUDATAIN), .in1(LED2), .out(DATAL1), .sel(LEDFEND));
  Multiplexer #(.width(15)) multiplexer_3 (.in0(CPUDATAIN), .in1(LED3), .out(DATAL2), .sel(LEDFEND));
  Multiplexer #(.width(15)) multiplexer_4 (.in0(CPUDATAIN), .in1(LED4), .out(DATAL3), .sel(LEDFEND));
  Multiplexer #(.width(15)) multiplexer_5 (.in0(CPUDATAIN), .in1(LED5), .out(DATAL4), .sel(LEDFEND));
  Multiplexer #(.select(4), .width(15)) multiplexer_6 (
    .in0(LED0), .in1(LED1), .in2(LED2), .in3(LED3), .in4(LED4), .in5(LED5), .in6(LED6), .in7(LED7),
    .in8(LED8), .in9(LED9), .in10(LEDA), .in11(LEDB), .in12(LEDC), .in13(LEDD), .in14(LEDE),
    .in15({15{1'b0}}), .out(LEDDATA), .sel(ADDR[3:0]));
  Multiplexer #(.width(15)) multiplexer_7 (.in0(CPUDATAIN), .in1(LED6), .out(DATAL5), .sel(LEDFEND));
  Multiplexer #(.width(15)) multiplexer_8 (.in0(CPUDATAIN), .in1(LED7), .out(DATAL6), .sel(LEDFEND));
  Multiplexer #(.width(15)) multiplexer_9 (.in0(CPUDATAIN), .in1(LED8), .out(DATAL7), .sel(LEDFEND));
  Multiplexer #(.width(15)) multiplexer_10 (.in0(CPUDATAIN), .in1(LED9), .out(DATAL8), .sel(LEDFEND));
  Multiplexer #(.width(15)) multiplexer_11 (.in0(CPUDATAIN), .in1(LEDA), .out(DATAL9), .sel(LEDFEND));
  and and_2 (LEDRE, RE, LEDCS);
  Multiplexer #(.width(15)) multiplexer_12 (.in0(CPUDATAIN), .in1(LEDB), .out(DATALA), .sel(LEDFEND));
  Multiplexer #(.width(15)) multiplexer_13 (.in0(CPUDATAIN), .in1(LEDC), .out(DATALB), .sel(LEDFEND));
  Multiplexer #(.width(15)) multiplexer_14 (.in0(CPUDATAIN), .in1(LEDD), .out(DATALC), .sel(LEDFEND));
  Multiplexer #(.width(15)) multiplexer_15 (.in0(CPUDATAIN), .in1(LEDE), .out(DATALD), .sel(LEDFEND));
  Multiplexer #(.width(15)) multiplexer_16 (.in0(CPUDATAIN), .in1(CPUDATAIN), .out(DATALE), .sel(LEDFEND));
  and and_3 (IOCS, ADDR[5], ADDR[6], ADDR[7], ADDR[8], ADDR[9], ADDR[10], ADDR[11], ADDR[12], ADDR[13], ADDR[14], 1'b1);
  and and_4 (TTYCS, IOCS, ADDR[0], ~ADDR[1], ~ADDR[2], ~ADDR[3], ADDR[4]);  // AND_Gate
  and and_5 (KBCS, IOCS, ~ADDR[0], ~ADDR[1], ~ADDR[2], ~ADDR[3], ADDR[4]);  // AND_Gate
  and and_6 (IVECTADDR, ADDR[0], ADDR[1], ADDR[2], ADDR[3], ADDR[4], ADDR[5], ADDR[6], ADDR[7], ADDR[8], ADDR[9], ADDR[10], ADDR[11], ADDR[12], ADDR[13], ADDR[14]);
  and and_7 (TTYWR, TTYCS, WE);
  and and_8 (and_8_out, TTYWR, DATA7);
  and and_9 (KBRD, KBCS, RE);
  and and_10 (and_10_out, KBCS, WE);
  Multiplexer multiplexer_17 (.in0(and_10_out), .in1(1'b0), .out(multiplexer_17_out), .sel(KBCLR));
  and and_11 (LEDCS, IOCS, ~ADDR[4], RWE);  // AND_Gate
  and and_12 (IVECTEN, IVECTADDR, WE);
  and and_13 (IVECTRE, IVECTADDR, RE);
  or or_16 (RWE, RE, WE);
  and and_14 (MEMCS, ~IOCS, RWE);  // AND_Gate
  Multiplexer multiplexer_18 (.in0(and_8_out), .in1(1'b0), .out(multiplexer_18_out), .sel(TTYCLR));
  D_Flip_Flop d_ff_1 (.clk(CLK), .D(multiplexer_17_out), .Q(KBCLR));  // open: Qn, preset, reset
  Register #(.width(15)) register_16 (.D(CPUDATAIN), .en(IVECTEN), .Q(IVECT), .clk(CLK));  // open: clr
  D_Flip_Flop d_ff_2 (.clk(CLK), .D(multiplexer_18_out), .Q(TTYCLR));  // open: Qn, preset, reset

  assign IRQ = KBIRQ;
  assign TTYDATA = CPUDATAIN[6:0];

  // Other names for the same wires on the sheet: DATA[14:0] = CPUDATAIN; KBDATA15[7:0] = {DATA7, KBDATA}
endmodule

module ADDER15 (
  input  CIN,
  input  [14:0] A,
  input  [14:0] B,
  output COUT,
  output [14:0] S
);

  wire and_1_out, and_2_out, and_3_out, and_4_out, and_5_out, and_6_out, and_7_out, and_8_out, and_9_out,
       and_10_out, and_11_out, and_12_out, and_13_out, and_14_out, and_15_out, and_16_out, and_17_out,
       and_18_out, and_19_out, and_20_out, and_21_out, and_22_out, and_23_out, and_24_out, and_25_out,
       and_26_out, and_27_out, and_28_out, and_29_out, and_30_out, C4, C9, or_1_out, or_2_out, or_3_out,
       or_4_out, or_6_out, or_7_out, or_8_out, or_9_out, or_11_out, or_12_out, or_13_out, or_14_out,
       xor_1_out, xor_2_out, xor_3_out, xor_4_out, xor_5_out, xor_11_out, xor_12_out, xor_13_out, xor_14_out,
       xor_15_out, xor_21_out, xor_22_out, xor_23_out, xor_24_out, xor_25_out;

  xor xor_1 (xor_1_out, A[0], B[0]);
  xor xor_2 (xor_2_out, A[1], B[1]);
  xor xor_3 (xor_3_out, A[2], B[2]);
  xor xor_4 (xor_4_out, A[3], B[3]);
  xor xor_5 (xor_5_out, A[4], B[4]);
  xor xor_6 (S[0], CIN, xor_1_out);
  and and_1 (and_1_out, CIN, xor_1_out);
  and and_2 (and_2_out, B[0], A[0]);
  xor xor_7 (S[1], or_1_out, xor_2_out);
  and and_3 (and_3_out, or_1_out, xor_2_out);
  and and_4 (and_4_out, B[1], A[1]);
  xor xor_8 (S[2], or_2_out, xor_3_out);
  and and_5 (and_5_out, or_2_out, xor_3_out);
  and and_6 (and_6_out, B[2], A[2]);
  xor xor_9 (S[3], or_3_out, xor_4_out);
  and and_7 (and_7_out, or_3_out, xor_4_out);
  and and_8 (and_8_out, B[3], A[3]);
  xor xor_10 (S[4], or_4_out, xor_5_out);
  or or_1 (or_1_out, and_1_out, and_2_out);
  or or_2 (or_2_out, and_3_out, and_4_out);
  or or_3 (or_3_out, and_5_out, and_6_out);
  or or_4 (or_4_out, and_7_out, and_8_out);
  and and_9 (and_9_out, or_4_out, xor_5_out);
  or or_5 (C4, and_9_out, and_10_out);
  and and_10 (and_10_out, B[4], A[4]);
  xor xor_11 (xor_11_out, A[5], B[5]);
  xor xor_12 (xor_12_out, A[6], B[6]);
  xor xor_13 (xor_13_out, A[7], B[7]);
  xor xor_14 (xor_14_out, A[8], B[8]);
  xor xor_15 (xor_15_out, A[9], B[9]);
  xor xor_16 (S[5], C4, xor_11_out);
  and and_11 (and_11_out, C4, xor_11_out);
  and and_12 (and_12_out, B[5], A[5]);
  xor xor_17 (S[6], or_6_out, xor_12_out);
  xor xor_18 (S[7], or_7_out, xor_13_out);
  and and_13 (and_13_out, or_7_out, xor_13_out);
  and and_14 (and_14_out, B[7], A[7]);
  xor xor_19 (S[8], or_8_out, xor_14_out);
  or or_6 (or_6_out, and_11_out, and_12_out);
  and and_15 (and_15_out, or_6_out, xor_12_out);
  or or_7 (or_7_out, and_15_out, and_16_out);
  and and_16 (and_16_out, B[6], A[6]);
  or or_8 (or_8_out, and_13_out, and_14_out);
  and and_17 (and_17_out, or_8_out, xor_14_out);
  or or_9 (or_9_out, and_17_out, and_18_out);
  and and_18 (and_18_out, B[8], A[8]);
  xor xor_20 (S[9], or_9_out, xor_15_out);
  and and_19 (and_19_out, or_9_out, xor_15_out);
  and and_20 (and_20_out, B[9], A[9]);
  or or_10 (C9, and_19_out, and_20_out);
  xor xor_21 (xor_21_out, A[10], B[10]);
  xor xor_22 (xor_22_out, A[11], B[11]);
  xor xor_23 (xor_23_out, A[12], B[12]);
  xor xor_24 (xor_24_out, A[13], B[13]);
  xor xor_25 (xor_25_out, A[14], B[14]);
  xor xor_26 (S[10], C9, xor_21_out);
  and and_21 (and_21_out, C9, xor_21_out);
  and and_22 (and_22_out, B[10], A[10]);
  xor xor_27 (S[11], or_11_out, xor_22_out);
  xor xor_28 (S[12], or_12_out, xor_23_out);
  and and_23 (and_23_out, or_12_out, xor_23_out);
  and and_24 (and_24_out, B[12], A[12]);
  xor xor_29 (S[13], or_13_out, xor_24_out);
  or or_11 (or_11_out, and_21_out, and_22_out);
  and and_25 (and_25_out, or_11_out, xor_22_out);
  or or_12 (or_12_out, and_25_out, and_26_out);
  and and_26 (and_26_out, B[11], A[11]);
  or or_13 (or_13_out, and_23_out, and_24_out);
  and and_27 (and_27_out, or_13_out, xor_24_out);
  or or_14 (or_14_out, and_27_out, and_28_out);
  and and_28 (and_28_out, B[13], A[13]);
  xor xor_30 (S[14], or_14_out, xor_25_out);
  and and_29 (and_29_out, or_14_out, xor_25_out);
  and and_30 (and_30_out, B[14], A[14]);
  or or_15 (COUT, and_29_out, and_30_out);
endmodule

module REGS15 (
  input  [14:0] D,
  input  W,
  input  [2:0] SelA,
  input  [2:0] SelB,
  input  [2:0] SelD,
  input  CLK,
  output [14:0] R0,
  output [14:0] R1,
  output [14:0] R2,
  output [14:0] R3,
  output [14:0] R4,
  output [14:0] R5,
  output [14:0] R6,
  output [14:0] R7,
  output [14:0] A,
  output [14:0] B
);

  wire demultiplexer_1_out0, demultiplexer_2_out0, demultiplexer_3_out0, demultiplexer_4_out0,
       demultiplexer_5_out0, demultiplexer_6_out0, demultiplexer_7_out0, W_R1, W_R2, W_R3, W_R4, W_R5, W_R6,
       W_R7;

  Demultiplexer #(.enable("true"), .select(3)) demultiplexer_1 (
    .out0(demultiplexer_1_out0), .out1(W_R1), .sel(SelD), .en(W));  // open: out2, out3, out4, out5, out6, out7, in
  Demultiplexer #(.enable("true"), .select(3)) demultiplexer_2 (
    .out0(demultiplexer_2_out0), .out2(W_R2), .sel(SelD), .en(W));  // open: out1, out3, out4, out5, out6, out7, in
  Demultiplexer #(.enable("true"), .select(3)) demultiplexer_3 (
    .out0(demultiplexer_3_out0), .out3(W_R3), .sel(SelD), .en(W));  // open: out1, out2, out4, out5, out6, out7, in
  Demultiplexer #(.enable("true"), .select(3)) demultiplexer_4 (
    .out0(demultiplexer_4_out0), .out4(W_R4), .sel(SelD), .en(W));  // open: out1, out2, out3, out5, out6, out7, in
  Demultiplexer #(.enable("true"), .select(3)) demultiplexer_5 (
    .out0(demultiplexer_5_out0), .out5(W_R5), .sel(SelD), .en(W));  // open: out1, out2, out3, out4, out6, out7, in
  Demultiplexer #(.enable("true"), .select(3)) demultiplexer_6 (
    .out0(demultiplexer_6_out0), .out6(W_R6), .sel(SelD), .en(W));  // open: out1, out2, out3, out4, out5, out7, in
  Demultiplexer #(.enable("true"), .select(3)) demultiplexer_7 (
    .out0(demultiplexer_7_out0), .out7(W_R7), .sel(SelD), .en(W));  // open: out1, out2, out3, out4, out5, out6, in
  Register #(.width(15)) register_1 (.D(D), .en(W_R1), .Q(R1), .clk(CLK));  // open: clr
  Register #(.width(15)) register_2 (.D(D), .en(W_R2), .Q(R2), .clk(CLK));  // open: clr
  Register #(.width(15)) register_3 (.D(D), .en(W_R3), .Q(R3), .clk(CLK));  // open: clr
  Register #(.width(15)) register_4 (.D(D), .en(W_R4), .Q(R4), .clk(CLK));  // open: clr
  Register #(.width(15)) register_5 (.D(D), .en(W_R5), .Q(R5), .clk(CLK));  // open: clr
  Register #(.width(15)) register_6 (.D(D), .en(W_R6), .Q(R6), .clk(CLK));  // open: clr
  Register #(.width(15)) register_7 (.D(D), .en(W_R7), .Q(R7), .clk(CLK));  // open: clr
  Multiplexer #(.select(3), .width(15)) multiplexer_1 (
    .in0({15{1'b0}}), .in1(R1), .in2(R2), .in3(R3), .in4(R4), .in5(R5), .in6(R6), .in7(R7), .out(A),
    .sel(SelA));
  Multiplexer #(.select(3), .width(15)) multiplexer_2 (
    .in0({15{1'b0}}), .in1(R1), .in2(R2), .in3(R3), .in4(R4), .in5(R5), .in6(R6), .in7(R7), .out(B),
    .sel(SelB));

  assign R0 = {15{1'b0}};
endmodule

module ALU15 (
  input  [14:0] A,
  input  [14:0] B,
  input  [2:0] OP,
  input  CIN,
  input  OIN,
  output C,
  output O,
  output N,
  output Z,
  output [14:0] R
);

  wire [0:0] multiplexer_11_out;
  wire [13:0] multiplexer_10_out_2, multiplexer_11_out_2;
  wire [14:0] multiplexer_2_out, multiplexer_3_out, multiplexer_4_out, multiplexer_6_out, multiplexer_7_out,
       multiplexer_8_out, multiplexer_9_out, not_1_out, R_ADD, R_AND, R_OR, R_SLL, R_SRA, R_SRL, R_SUB, R_XOR;
  wire [14:14] multiplexer_10_out;

  assign R_AND = A & B;  // AND_Gate and_1, 15 bits wide
  assign R_OR = A | B;  // OR_Gate or_1, 15 bits wide
  assign R_XOR = A ^ B;  // XOR_Gate xor_1, 15 bits wide
  Multiplexer #(.select(3), .width(15)) multiplexer_1 (
    .in0(R_ADD), .in1(R_SUB), .in2(R_AND), .in3(R_OR), .in4(R_XOR), .in5(R_SLL), .in6(R_SRL), .in7(R_SRA),
    .out(R), .sel(OP));
  ADDER15 adder15_1 (.CIN(CIN), .A(A), .B(B), .S(R_ADD), .COUT(OIN));
  Multiplexer #(.width(15)) multiplexer_2 (.in0(A), .in1({{8{1'b1}}, A[14:8]}), .out(multiplexer_2_out), .sel(B[3]));
  Multiplexer #(.width(15)) multiplexer_3 (
    .in0({4'b1111, multiplexer_2_out[14:4]}), .in1(multiplexer_2_out), .out(multiplexer_3_out), .sel(B[2]));
  Multiplexer #(.width(15)) multiplexer_4 (
    .in0({2'b11, multiplexer_3_out[14:2]}), .in1(multiplexer_3_out), .out(multiplexer_4_out), .sel(B[1]));
  assign not_1_out = ~B;  // NOT_Gate not_1, 15 bits wide
  ADDER15 adder15_2 (.CIN(CIN), .A(A), .B(not_1_out), .S(R_SUB), .COUT(OIN));
  Multiplexer #(.width(15)) multiplexer_5 (
    .in0({1'b1, multiplexer_4_out[14:1]}), .in1(multiplexer_4_out), .out(R_SRA), .sel(B[0]));
  Multiplexer #(.width(15)) multiplexer_6 (.in0(A), .in1({A[6:0], {8{1'b0}}}), .out(multiplexer_6_out), .sel(B[3]));
  Multiplexer #(.width(15)) multiplexer_7 (.in0(A), .in1({{8{1'b0}}, A[14:8]}), .out(multiplexer_7_out), .sel(B[3]));
  Multiplexer #(.width(15)) multiplexer_8 (
    .in0({multiplexer_6_out[10:0], 4'b0000}), .in1(multiplexer_6_out), .out(multiplexer_8_out), .sel(B[2]));
  Multiplexer #(.width(15)) multiplexer_9 (
    .in0({4'b0000, multiplexer_7_out[14:4]}), .in1(multiplexer_7_out), .out(multiplexer_9_out), .sel(B[2]));
  Multiplexer #(.width(15)) multiplexer_10 (
    .in0({multiplexer_8_out[12:0], 2'b00}), .in1(multiplexer_8_out),
    .out({multiplexer_10_out[14], multiplexer_10_out_2}), .sel(B[1]));
  Multiplexer #(.width(15)) multiplexer_11 (
    .in0({2'b00, multiplexer_9_out[14:2]}), .in1(multiplexer_9_out),
    .out({multiplexer_11_out_2, multiplexer_11_out[0]}), .sel(B[1]));
  Multiplexer #(.width(15)) multiplexer_12 (
    .in0({multiplexer_10_out_2, 1'b0}), .in1({multiplexer_10_out[14], multiplexer_10_out_2}), .out(R_SLL),
    .sel(B[0]));
  Multiplexer #(.width(15)) multiplexer_13 (
    .in0({1'b0, multiplexer_11_out_2}), .in1({multiplexer_11_out_2, multiplexer_11_out[0]}), .out(R_SRL),
    .sel(B[0]));
  Multiplexer #(.select(3)) multiplexer_14 (
    .in0(1'b1), .in1(1'b1), .in2(1'b0), .in3(1'b0), .in4(1'b0), .in5(1'b1), .in6(1'b1), .in7(1'b1), .out(C),
    .sel(OP));
  Multiplexer #(.select(3)) multiplexer_15 (
    .in0(1'b1), .in1(1'b1), .in2(1'b0), .in3(1'b0), .in4(1'b0), .in5(1'b0), .in6(1'b0), .in7(1'b0), .out(O),
    .sel(OP));
  Multiplexer #(.select(3)) multiplexer_16 (
    .in0(1'b1), .in1(1'b1), .in2(1'b1), .in3(1'b1), .in4(1'b1), .in5(1'b1), .in6(1'b1), .in7(1'b1), .out(N),
    .sel(OP));
  Multiplexer #(.select(3)) multiplexer_17 (
    .in0(1'b1), .in1(1'b1), .in2(1'b1), .in3(1'b1), .in4(1'b1), .in5(1'b1), .in6(1'b1), .in7(1'b1), .out(Z),
    .sel(OP));

  // Other names for the same wires on the sheet: SUB = OP[0]

  // Notes on the sheet:
  //   AND 00010
  //   OR 00011
  //   XOR 00100
  //   ADD 00000
  //   SUB 00001
  //   SRA 00111
  //   SLL 00101
  //   SRL 00110
endmodule

module FLAGS8 (
  input  in_1,
  input  [7:0] in_2,
  input  [7:0] in_3,
  input  in_4,
  output [7:0] out_5
);

  wire multiplexer_1_out, multiplexer_2_out, multiplexer_3_out, multiplexer_4_out, multiplexer_5_out,
       multiplexer_6_out, multiplexer_7_out, multiplexer_8_out, or_1_out, or_2_out, or_3_out, or_4_out,
       or_5_out, or_6_out, or_7_out, or_8_out;

  Multiplexer multiplexer_1 (.in0(out_5[0]), .in1(in_2[0]), .out(multiplexer_1_out), .sel(in_3[0]));
  Multiplexer multiplexer_2 (.in0(out_5[1]), .in1(in_2[1]), .out(multiplexer_2_out), .sel(in_3[1]));
  Multiplexer multiplexer_3 (.in0(out_5[2]), .in1(in_2[2]), .out(multiplexer_3_out), .sel(in_3[2]));
  Multiplexer multiplexer_4 (.in0(out_5[3]), .in1(in_2[3]), .out(multiplexer_4_out), .sel(in_3[3]));
  or or_1 (or_1_out, multiplexer_1_out, in_1);
  or or_2 (or_2_out, multiplexer_2_out, in_1);
  or or_3 (or_3_out, multiplexer_3_out, in_1);
  or or_4 (or_4_out, multiplexer_4_out, in_1);
  D_Flip_Flop d_ff_1 (.D(or_1_out), .clk(in_4), .Q(out_5[0]));  // open: Qn, preset, reset
  D_Flip_Flop d_ff_2 (.D(or_2_out), .clk(in_4), .Q(out_5[1]));  // open: Qn, preset, reset
  D_Flip_Flop d_ff_3 (.D(or_3_out), .clk(in_4), .Q(out_5[2]));  // open: Qn, preset, reset
  D_Flip_Flop d_ff_4 (.D(or_4_out), .clk(in_4), .Q(out_5[3]));  // open: Qn, preset, reset
  Multiplexer multiplexer_5 (.in0(out_5[4]), .in1(in_2[4]), .out(multiplexer_5_out), .sel(in_3[4]));
  Multiplexer multiplexer_6 (.in0(out_5[5]), .in1(in_2[5]), .out(multiplexer_6_out), .sel(in_3[5]));
  Multiplexer multiplexer_7 (.in0(out_5[6]), .in1(in_2[2]), .out(multiplexer_7_out), .sel(in_3[6]));
  Multiplexer multiplexer_8 (.in0(out_5[7]), .in1(in_2[7]), .out(multiplexer_8_out), .sel(in_3[7]));
  D_Flip_Flop d_ff_5 (.D(or_5_out), .clk(in_4), .Q(out_5[4]));  // open: Qn, preset, reset
  or or_5 (or_5_out, multiplexer_5_out, in_1);
  D_Flip_Flop d_ff_6 (.D(or_6_out), .clk(in_4), .Q(out_5[5]));  // open: Qn, preset, reset
  or or_6 (or_6_out, multiplexer_6_out, in_1);
  D_Flip_Flop d_ff_7 (.D(or_7_out), .clk(in_4), .Q(out_5[6]));  // open: Qn, preset, reset
  or or_7 (or_7_out, multiplexer_7_out, in_1);
  D_Flip_Flop d_ff_8 (.D(or_8_out), .clk(in_4), .Q(out_5[7]));  // open: Qn, preset, reset
  or or_8 (or_8_out, multiplexer_8_out, in_1);

  // Other names for the same wires on the sheet: CLK = in_4; F[7:0] = out_5; F0 = out_5[0]; F1 = out_5[1];
  //   F2 = out_5[2]; F3 = out_5[3]; F4 = out_5[4]; F5 = out_5[5]; F6 = out_5[6]; F7 = out_5[7]; IRQ = in_1;
  //   NF[7:0] = in_2; NF0 = in_2[0]; NF1 = in_2[1]; NF2 = in_2[2]; NF3 = in_2[3]; NF4 = in_2[4]; NF5 = in_2[5];
  //   NF6 = in_2[6]; NF7 = in_2[7]; WM[7:0] = in_3; WM0 = in_3[0]; WM1 = in_3[1]; WM2 = in_3[2]; WM3 = in_3[3];
  //   WM4 = in_3[4]; WM5 = in_3[5]; WM6 = in_3[6]; WM7 = in_3[7]
endmodule

module IMM15 (
  input  [14:0] INST,
  output [14:0] SEXT
);

  wire [14:0] multiplexer_1_out;

  Multiplexer #(.select(3), .width(15)) multiplexer_1 (
    .in0({15{1'b0}}), .in1({15{1'b0}}), .in2({15{1'b0}}), .in3({{12{INST[14]}}, INST[13:11]}),
    .in4({{9{INST[14]}}, INST[13:8]}), .in5({{9{INST[14]}}, INST[13:8]}), .in6({{13{INST[7]}}, INST[6:5]}),
    .in7({{9{INST[14]}}, INST[13:8]}), .out(multiplexer_1_out), .sel(INST[2:0]));
  Multiplexer #(.select(2), .width(15)) multiplexer_2 (
    .in0({15{1'b0}}), .in1({{12{INST[14]}}, INST[13:11]}), .in2({{6{INST[14]}}, INST[13:5]}),
    .in3(multiplexer_1_out), .out(SEXT), .sel(INST[4:3]));

  // Other names for the same wires on the sheet: I_20[14:0] = {{13{INST[7]}}, INST[6:5]};
  //   I_90[14:0] = {{6{INST[14]}}, INST[13:5]}; IMM20[2:0] = INST[7:5]; IMM90[9:0] = INST[14:5];
  //   I_60[14:0] = {{9{INST[14]}}, INST[13:8]}; I_104[14:0] = {{9{INST[14]}}, INST[13:8]}; IMM60[6:0] = INST[14:8];
  //   IMM104[6:0] = INST[14:8]; I_30[14:0] = {{12{INST[14]}}, INST[13:11]}; IMM30[3:0] = INST[14:11];
  //   INST45[1:0] = INST[4:3]; INST123[2:0] = INST[2:0]
endmodule

module DECODE15 (
  input  [4:0] OPCODE,
  output SWI,
  output STORE,
  output LOAD,
  output [1:0] ASEL,
  output [1:0] BSEL,
  output [2:0] ALUOP,
  output [2:0] REGDATASRC,
  output REGW,
  output [1:0] FLAGSRC,
  output [7:0] FLAGWM,
  output SRPW,
  output SRFW
);

  wire FORCE_ADD, Load_t;

  and and_1 (Load_t, OPCODE[0], ~OPCODE[1], ~OPCODE[2], OPCODE[3], ~OPCODE[4]);  // AND_Gate
  Multiplexer #(.width(3)) multiplexer_1 (.in0(OPCODE[2:0]), .in1(3'b000), .out(ALUOP), .sel(FORCE_ADD));
  or or_1 (FORCE_ADD, Load_t, OPCODE[4]);
  ROM #(.addrWidth(5), .dataWidth(23)) rom_1 (
    .addr(OPCODE), .data({SRFW, SRPW, FLAGWM, FLAGSRC, REGW, REGDATASRC, BSEL, ASEL, LOAD, STORE, SWI}));

  // Other names for the same wires on the sheet: OPCODE_2_0[2:0] = OPCODE[2:0]

  // Notes on the sheet:
  //   contents of rom_1 (hex, n*v repeats v):
  //   8*103c 8*1103c 6*50000 103c 210000 210000 210000 21000 50000 50000 210000 210000 11000
endmodule
